// Logisim project gates.circ as structural Verilog: 1 circuit, main circuit main
module main (
  input  a,
  input  b,
  input  c,
  input  d,
  input  e,
  input  f,
  output x
);

  wire and_1_out, and_2_out, and_3_out, and_4_out, and_5_out, and_6_out, nand_1_out, nor_1_out, not_1_out,
       not_2_out, or_1_out, xor_1_out, xor_2_out, xor_3_out;

  not not_1 (not_1_out, a);
  not not_2 (not_2_out, c);
  or or_1 (or_1_out, b, c);
  and and_1 (and_1_out, not_1_out, f);
  and and_2 (and_2_out, or_1_out, not_2_out);
  xor xor_1 (xor_1_out, d, e);
  and and_3 (and_3_out, and_1_out, and_2_out);
  xor xor_2 (xor_2_out, xor_1_out, and_3_out);
  and and_4 (and_4_out, xor_2_out, f);
  xor xor_3 (xor_3_out, and_4_out, e);
  nor nor_1 (nor_1_out, d, a);
  nand nand_1 (nand_1_out, b, e);
  and and_5 (and_5_out, xor_3_out, nor_1_out);
  and and_6 (and_6_out, nand_1_out, c);
  and and_7 (x, and_5_out, and_6_out);
endmodule
